# Fritzing sketch Most (saved by Fritzing 0.9.3b)
circuit board: 8.46667cm x 5.64444cm
breadboards: 1

parts:
  Croduino_Basic1 = Croduino Basic2
  R1 = Resistor [tolerance=±5% resistance=330 package=THT]
  R4 = Resistor [tolerance=±5% resistance=220 package=THT]
  R5 = Resistor [tolerance=±5% resistance=220 package=THT]
  R6 = Resistor [tolerance=±5% resistance=220 package=THT]
  R7 = Resistor [tolerance=±5% resistance=220 package=THT]
  R8 = Resistor [tolerance=±5% resistance=220 package=THT]
  R9 = Resistor [tolerance=±5% resistance=220 package=THT]
  R10 = Resistor [tolerance=±5% resistance=330 package=THT]
  R11 = Resistor [tolerance=±5% resistance=330 package=THT]
  R12 = Resistor [tolerance=±5% resistance=330 package=THT]
  R13 = Resistor [tolerance=±5% resistance=330 package=THT]
  R14 = Resistor [tolerance=±5% resistance=330 package=THT]
  LEDBRR12 = LED - 5mm [color="Red (633nm)" package="5 mm [THT]"]
  LEDBRR11 = LED - 5mm [color="Red (633nm)" package="5 mm [THT]"]
  LEDBRR21 = LED - 5mm [color="Red (633nm)" package="5 mm [THT]"]
  LEDBRR22 = LED - 5mm [color="Red (633nm)" package="5 mm [THT]"]
  LEDBRR31 = LED - 5mm [color="Red (633nm)" package="5 mm [THT]"]
  LEDBRR32 = LED - 5mm [color="Red (633nm)" package="5 mm [THT]"]
  LEDBRL31 = LED - 5mm [color="Red (633nm)" package="5 mm [THT]"]
  LEDBRL32 = LED - 5mm [color="Red (633nm)" package="5 mm [THT]"]
  LEDBRL22 = LED - 5mm [color="Red (633nm)" package="5 mm [THT]"]
  LEDBRL21 = LED - 5mm [color="Red (633nm)" package="5 mm [THT]"]
  LEDBRL12 = LED - 5mm [color="Red (633nm)" package="5 mm [THT]"]
  LEDBRL11 = LED - 5mm [color="Red (633nm)" package="5 mm [THT]"]
  LEDRL = LED - 3mm [color="Red (633nm)" package="3 mm [THT]"]
  LEDGL = LED - 3mm [color="Green (555nm)" package="3 mm [THT]"]
  LEDRR = LED - 3mm [color="Red (633nm)" package="3 mm [THT]"]
  LEDGR = LED - 3mm [color="Green (555nm)" package="3 mm [THT]"]
  BUZZER-R = Piezo Speaker
  BUZZER-L = Piezo Speaker
  BARRIER-R = Tower Pro SG90 servo [part_number=101246]
  BRIDGE-R = Tower Pro SG90 servo [part_number=101246]
  BRIDGE-L = Tower Pro SG90 servo [part_number=101246]
  BARRIER-L = Tower Pro SG90 servo [part_number=101246]
  IR-SENSOR-EXIT = TSOP312.., 314.. [package=THT]
  IR-LED-EXIT = LED - 5mm [color="Infrared (850nm)" package="5 mm [THT]"]
  IR-SENSOR-ENTRY = TSOP312.., 314.. [package=THT]
  IR-LED-ENTRY = LED - 5mm [color="Infrared (850nm)" package="5 mm [THT]"]

nets:
  N1: Croduino_Basic1.D12_/_MISO, R11.Pin_0, R14.Pin_0
  N2: Croduino_Basic1.D9_/PWM, BRIDGE-R.Signal, BRIDGE-L.Signal
  N3: Croduino_Basic1.D8, R10.Pin_0, R13.Pin_0
  N4: Croduino_Basic1.D7, R1.Pin_0, R12.Pin_0
  N5: Croduino_Basic1.D6_/PWM, BARRIER-R.Signal, BARRIER-L.Signal
  N6: Croduino_Basic1.D4, IR-SENSOR-EXIT.Data
  N7: Croduino_Basic1.D2, IR-SENSOR-ENTRY.Data
  N8: Croduino_Basic1.A5_/SCL, R7.Pin_0
  N9: Croduino_Basic1.A4_/SDA, R9.Pin_0
  N10: Croduino_Basic1.A3, R8.Pin_0
  N11: Croduino_Basic1.A2, R6.Pin_0
  N12: Croduino_Basic1.A1, R5.Pin_0
  N13: Croduino_Basic1.A0, R4.Pin_0
  +5V: Croduino_Basic1.+5V, BARRIER-R.+5V, BRIDGE-R.+5V, BRIDGE-L.+5V, BARRIER-L.+5V, IR-SENSOR-EXIT.Vs, IR-LED-EXIT.anode, IR-SENSOR-ENTRY.Vs, IR-LED-ENTRY.anode
  GND: Croduino_Basic1.gnd, LEDBRR12.cathode, LEDBRR11.cathode, LEDBRR21.cathode, LEDBRR22.cathode, LEDBRR31.cathode, LEDBRR32.cathode, LEDBRL31.cathode, LEDBRL32.cathode, LEDBRL22.cathode, LEDBRL21.cathode, LEDBRL12.cathode, LEDBRL11.cathode, LEDRL.cathode, LEDGL.cathode, LEDRR.cathode, LEDGR.cathode, BUZZER-R.pin1, BUZZER-L.pin1, BARRIER-R.GND, BRIDGE-R.GND, BRIDGE-L.GND, BARRIER-L.GND, IR-SENSOR-EXIT.GND, IR-LED-EXIT.cathode, IR-SENSOR-ENTRY.GND, IR-LED-ENTRY.cathode
  N14: R1.Pin_1, LEDRR.anode
  N15: R4.Pin_1, LEDBRL12.anode, LEDBRL11.anode
  N16: R5.Pin_1, LEDBRL22.anode, LEDBRL21.anode
  N17: R6.Pin_1, LEDBRL31.anode, LEDBRL32.anode
  N18: R7.Pin_1, LEDBRR12.anode, LEDBRR11.anode
  N19: R8.Pin_1, LEDBRR31.anode, LEDBRR32.anode
  N20: R9.Pin_1, LEDBRR21.anode, LEDBRR22.anode
  N21: R10.Pin_1, LEDGR.anode
  N22: R11.Pin_1, BUZZER-R.pin2
  N23: R12.Pin_1, LEDRL.anode
  N24: R13.Pin_1, LEDGL.anode
  N25: R14.Pin_1, BUZZER-L.pin2

custom parts:
  Croduino Basic2: Croduino Basic2 is an Arduino compatible development board with ATmega328 and CP2102.
  Tower Pro SG90 servo: Original file by John De Cristofaro http://www.adafruit.com/products/1449 Adafruit Feedback Servo (Small) Edited by: e-radionica.com 28/9/2015
